// Logisim project alu_assignment.circ as structural Verilog: 2 circuits, main circuit IC_Diagram
module main (
  input  CS2,
  input  CS1,
  input  [3:0] A,
  input  [3:0] B,
  input  cs0,
  output Z,
  output [3:0] out_7,
  output C,
  output S,
  output V
);

  wire adder_1_cout, adder_1_out, adder_2_cout, adder_2_out, adder_3_cout, adder_3_out, adder_4_cout,
       adder_4_out, and_1_out, and_2_out, multiplexer_1_out, multiplexer_2_out, multiplexer_3_out,
       multiplexer_4_out, not_1_out, not_2_out, not_3_out, not_4_out, not_6_out, or_1_out, or_2_out,
       or_3_out, or_4_out, or_5_out, or_6_out, or_7_out, or_9_out, or_10_out, xor_1_out, xor_2_out,
       xor_3_out, xor_4_out, xor_5_out, xor_6_out, xor_7_out, xor_8_out, xor_9_out, xor_10_out, xor_11_out,
       Y3;

  not not_1 (not_1_out, CS2);
  not not_2 (not_2_out, CS1);
  and and_1 (and_1_out, not_1_out, CS1);
  xor xor_1 (xor_1_out, B[0], CS1);
  xor xor_2 (xor_2_out, B[1], CS1);
  xor xor_3 (xor_3_out, B[2], CS1);
  xor xor_4 (xor_4_out, B[3], CS1);
  or or_1 (or_1_out, A[0], B[0]);
  xor xor_5 (xor_5_out, B[0], A[0]);
  or or_2 (or_2_out, A[1], B[1]);
  xor xor_6 (xor_6_out, B[1], A[1]);
  or or_3 (or_3_out, A[2], B[2]);
  xor xor_7 (xor_7_out, B[2], A[2]);
  or or_4 (or_4_out, A[3], B[3]);
  xor xor_8 (xor_8_out, B[3], A[3]);
  and and_2 (and_2_out, not_1_out, not_2_out);
  or or_5 (or_5_out, and_1_out, xor_1_out);
  or or_6 (or_6_out, and_1_out, xor_2_out);
  or or_7 (or_7_out, and_1_out, xor_3_out);
  or or_8 (Y3, and_1_out, xor_4_out);
  Multiplexer #(.enable("false")) multiplexer_1 (.in0(or_1_out), .in1(xor_5_out), .out(multiplexer_1_out), .sel(cs0));
  Multiplexer #(.enable("false")) multiplexer_2 (.in0(or_2_out), .in1(xor_6_out), .out(multiplexer_2_out), .sel(cs0));
  Multiplexer #(.enable("false")) multiplexer_3 (.in0(or_3_out), .in1(xor_7_out), .out(multiplexer_3_out), .sel(cs0));
  Multiplexer #(.enable("false")) multiplexer_4 (.in0(or_4_out), .in1(xor_8_out), .out(multiplexer_4_out), .sel(cs0));
  Adder #(.width(1)) adder_1 (.a(A[0]), .b(or_5_out), .out(adder_1_out), .cin(and_2_out), .cout(adder_1_cout));
  Adder #(.width(1)) adder_2 (.a(A[1]), .b(or_6_out), .out(adder_2_out), .cin(adder_1_cout), .cout(adder_2_cout));
  Adder #(.width(1)) adder_3 (.a(A[2]), .b(or_7_out), .out(adder_3_out), .cin(adder_2_cout), .cout(adder_3_cout));
  Adder #(.width(1)) adder_4 (.a(A[3]), .b(Y3), .out(adder_4_out), .cin(adder_3_cout), .cout(adder_4_cout));
  xor xor_9 (xor_9_out, CS1, cs0);
  Multiplexer #(.enable("false")) multiplexer_5 (
    .in0(adder_1_out), .in1(multiplexer_1_out), .out(out_7[0]), .sel(xor_9_out));
  Multiplexer #(.enable("false")) multiplexer_6 (
    .in0(adder_2_out), .in1(multiplexer_2_out), .out(out_7[1]), .sel(xor_9_out));
  Multiplexer #(.enable("false")) multiplexer_7 (
    .in0(adder_3_out), .in1(multiplexer_3_out), .out(out_7[2]), .sel(xor_9_out));
  Multiplexer #(.enable("false")) multiplexer_8 (
    .in0(adder_4_out), .in1(multiplexer_4_out), .out(out_7[3]), .sel(xor_9_out));
  not not_3 (not_3_out, xor_9_out);
  xor xor_10 (xor_10_out, adder_4_out, A[3]);
  xor xor_11 (xor_11_out, A[3], Y3);
  not not_4 (not_4_out, xor_10_out);
  or or_9 (or_9_out, not_4_out, xor_11_out);
  not not_5 (Z, or_10_out);
  or or_10 (or_10_out, out_7[0], out_7[1], out_7[2], out_7[3]);
  and and_3 (C, adder_4_cout, not_3_out);
  and and_4 (V, not_6_out, not_3_out);
  not not_6 (not_6_out, or_9_out);

  assign S = out_7[3];
endmodule

module IC_Diagram (
  input  CS0,
  input  CS1,
  input  CS2,
  input  [3:0] A,
  input  [3:0] B,
  output [3:0] out_6,
  output C,
  output S,
  output V,
  output Z
);

  wire CS1_C, CS2_C, dip_74283_1_y1, dip_74283_1_y2, dip_74283_1_y3, dip_74283_1_y4, l_7408_56b2d8cc_1_p3,
       l_7408_56b2d8cc_1_p9, l_7408_56b2d8cc_1_p10, l_7408_56b2d8cc_1_p13, l_7432_b48b1b0f_1_p3,
       l_7432_b48b1b0f_1_p6, l_7432_b48b1b0f_1_p11, l_7432_b48b1b0f_1_p14, l_7432_b48b1b0f_2_p1,
       l_7432_b48b1b0f_2_p3, l_7432_b48b1b0f_2_p6, l_7432_b48b1b0f_2_p14, l_7432_b48b1b0f_3_p3,
       l_7432_b48b1b0f_3_p6, l_7432_b48b1b0f_3_p10, l_7432_b48b1b0f_3_p11, l_7432_b48b1b0f_3_p14,
       l_7486_91cf6df9_1_p3, l_7486_91cf6df9_1_p6, l_7486_91cf6df9_1_p11, l_7486_91cf6df9_1_p14,
       l_7486_91cf6df9_2_p3, l_7486_91cf6df9_2_p6, l_7486_91cf6df9_2_p11, l_7486_91cf6df9_2_p14,
       l_7486_91cf6df9_3_p8, l_7486_91cf6df9_3_p11, l_74157_eb3a92a2_1_p4, l_74157_eb3a92a2_1_p7,
       l_74157_eb3a92a2_1_p13, l_74157_eb3a92a2_1_p16, l_74157_eb3a92a2_2_p1, Y3;

  // L_7432_b48b1b0f l_7432_b48b1b0f_1: pin names not known; wires that end beside it: B[0], A[0], l_7432_b48b1b0f_1_p3, B[1], A[1], l_7432_b48b1b0f_1_p6, 1'b0, 1'b1, B[3], A[3], l_7432_b48b1b0f_1_p11, A[2], B[2], l_7432_b48b1b0f_1_p14
  // L_7486_91cf6df9 l_7486_91cf6df9_1: pin names not known; wires that end beside it: CS1, B[0], l_7486_91cf6df9_1_p3, CS1, B[1], l_7486_91cf6df9_1_p6, 1'b0, 1'b1, CS1, B[3], l_7486_91cf6df9_1_p11, CS1, B[2], l_7486_91cf6df9_1_p14
  // L_7486_91cf6df9 l_7486_91cf6df9_2: pin names not known; wires that end beside it: B[0], A[0], l_7486_91cf6df9_2_p3, B[1], A[1], l_7486_91cf6df9_2_p6, 1'b0, 1'b1, B[3], A[3], l_7486_91cf6df9_2_p11, B[2], A[2], l_7486_91cf6df9_2_p14
  // L_7432_b48b1b0f l_7432_b48b1b0f_2: pin names not known; wires that end beside it: l_7432_b48b1b0f_2_p1, l_7486_91cf6df9_1_p3, l_7432_b48b1b0f_2_p3, l_7432_b48b1b0f_2_p1, l_7486_91cf6df9_1_p6, l_7432_b48b1b0f_2_p6, 1'b0, 1'b1, l_7432_b48b1b0f_2_p1, l_7486_91cf6df9_1_p11, Y3, l_7432_b48b1b0f_2_p1, l_7486_91cf6df9_1_p14, l_7432_b48b1b0f_2_p14
  // L_7408_56b2d8cc l_7408_56b2d8cc_1: pin names not known; wires that end beside it: CS1_C, CS2_C, l_7408_56b2d8cc_1_p3, CS1, CS2_C, l_7432_b48b1b0f_2_p1, 1'b0, 1'b1, l_7408_56b2d8cc_1_p9, l_7408_56b2d8cc_1_p10, V, l_7408_56b2d8cc_1_p9, l_7408_56b2d8cc_1_p13, C
  // L_74157_eb3a92a2 l_74157_eb3a92a2_1: pin names not known; wires that end beside it: CS0, l_7432_b48b1b0f_1_p3, l_7486_91cf6df9_2_p3, l_74157_eb3a92a2_1_p4, l_7432_b48b1b0f_1_p6, l_7486_91cf6df9_2_p6, l_74157_eb3a92a2_1_p7, 1'b0, 1'b1, 1'b0, l_7432_b48b1b0f_1_p11, l_7486_91cf6df9_2_p11, l_74157_eb3a92a2_1_p13, l_7432_b48b1b0f_1_p14, l_7486_91cf6df9_2_p14, l_74157_eb3a92a2_1_p16
  DIP_74283 dip_74283_1 (
    .CIN(l_7408_56b2d8cc_1_p3), .A1(A[0]), .B1(l_7432_b48b1b0f_2_p3), .A2(A[1]), .B2(l_7432_b48b1b0f_2_p6),
    .A3(A[2]), .B3(l_7432_b48b1b0f_2_p14), .A4(A[3]), .B4(Y3), .Y1(dip_74283_1_y1), .Y2(dip_74283_1_y2),
    .Y3(dip_74283_1_y3), .Y4(dip_74283_1_y4), .COUT(l_7408_56b2d8cc_1_p13));
  // L_74157_eb3a92a2 l_74157_eb3a92a2_2: pin names not known; wires that end beside it: l_74157_eb3a92a2_2_p1, dip_74283_1_y1, l_74157_eb3a92a2_1_p4, out_6[0], dip_74283_1_y2, l_74157_eb3a92a2_1_p7, out_6[1], 1'b0, 1'b1, 1'b0, dip_74283_1_y4, l_74157_eb3a92a2_1_p13, out_6[3], dip_74283_1_y3, l_74157_eb3a92a2_1_p16, out_6[2]
  // L_7486_91cf6df9 l_7486_91cf6df9_3: pin names not known; wires that end beside it: CS1, CS0, l_74157_eb3a92a2_2_p1, 1'b0, 1'b1, A[3], Y3, l_7486_91cf6df9_3_p8, A[3], dip_74283_1_y4, l_7486_91cf6df9_3_p11
  // L_7432_b48b1b0f l_7432_b48b1b0f_3: pin names not known; wires that end beside it: out_6[0], out_6[1], l_7432_b48b1b0f_3_p3, out_6[2], out_6[3], l_7432_b48b1b0f_3_p6, 1'b0, 1'b1, l_7486_91cf6df9_3_p8, l_7432_b48b1b0f_3_p10, l_7432_b48b1b0f_3_p11, l_7432_b48b1b0f_3_p3, l_7432_b48b1b0f_3_p6, l_7432_b48b1b0f_3_p14
  // L_7404_c2a15244 l_7404_c2a15244_1: pin names not known; wires that end beside it: l_74157_eb3a92a2_2_p1, l_7408_56b2d8cc_1_p9, l_7432_b48b1b0f_3_p14, Z, l_7486_91cf6df9_3_p11, l_7432_b48b1b0f_3_p10, 1'b0, 1'b1, CS1, CS1_C, CS2, CS2_C, l_7432_b48b1b0f_3_p11, l_7408_56b2d8cc_1_p10

  assign S = out_6[3];

  // Notes on the sheet:
  //   CS2'CS1
  //   S0
  //   S1
  //   S3
  //   S3
  //   S2
  //   S2
  //   XOR(CS1,CS0)_C
  //   XOR(CS1,CS0)_C
endmodule
