// Logisim project assignment2 (2).circ as structural Verilog: 5 circuits, main circuit FP_adder_main
module FP_adder_main (
  input  [15:0] A,
  input  [15:0] B,
  output underflow_flag,
  output overflow_flag,
  output [15:0] finaloutput
);

  wire add_sub_sig_1_operation_sign, adder_1_cout, and_1_out, exponent_compare_1_a_is_smaller, or_1_out;
  wire [4:0] exponent_compare_1_abs_difference, exponent_compare_1_current_big_exponent,
       normalized_1_normalized_exponent;
  wire [13:0] align_significands_1_aligned_sig_b, align_significands_1_alligned_sig_a,
       normalized_1_normalized_fraction;
  wire [14:0] add_sub_sig_1_alu_fraction_in;

  exponent_compare exponent_compare_1 (
    .exponent_a(A[14:10]), .exponent_b(B[14:10]),
    .current_big_exponent(exponent_compare_1_current_big_exponent),
    .a_is_smaller(exponent_compare_1_a_is_smaller), .abs_difference(exponent_compare_1_abs_difference));
  align_significands align_significands_1 (
    .sig_a({1'b1, A[9:0]}), .a_is_smaller(exponent_compare_1_a_is_smaller),
    .abs_diff(exponent_compare_1_abs_difference), .sig_b({1'b1, B[9:0]}),
    .alligned_sig_a(align_significands_1_alligned_sig_a), .aligned_sig_b(align_significands_1_aligned_sig_b));
  add_sub_sig add_sub_sig_1 (
    .sign_of_a(A[15]), .sign_of_b(B[15]), .a_alligned(align_significands_1_alligned_sig_a),
    .b_alligned(align_significands_1_aligned_sig_b), .result_sign(finaloutput[15]),
    .operation_sign(add_sub_sig_1_operation_sign), .alu_fraction_in(add_sub_sig_1_alu_fraction_in));  // open: result_sig, carry_out
  or or_1 (or_1_out, normalized_1_normalized_fraction[0], normalized_1_normalized_fraction[3], normalized_1_normalized_fraction[1]);
  and and_1 (and_1_out, or_1_out, normalized_1_normalized_fraction[2]);
  normalized normalized_1 (
    .ALU_Fraction_In(add_sub_sig_1_alu_fraction_in),
    .Current_Exponent(exponent_compare_1_current_big_exponent), .result_sign(add_sub_sig_1_operation_sign),
    .Normalized_Fraction(normalized_1_normalized_fraction),
    .Normalized_Exponent(normalized_1_normalized_exponent), .underflow(underflow_flag),
    .overflow(overflow_flag));
  Adder #(.width(10)) adder_1 (
    .a(normalized_1_normalized_fraction[12:3]), .b({10{1'b0}}), .out(finaloutput[9:0]), .cin(and_1_out),
    .cout(adder_1_cout));
  Adder #(.width(5)) adder_2 (
    .a(normalized_1_normalized_exponent), .b({5{1'b0}}), .out(finaloutput[14:10]), .cin(adder_1_cout));  // open: cout
endmodule

module exponent_compare (
  input  [4:0] exponent_a,
  input  [4:0] exponent_b,
  output [4:0] current_big_exponent,
  output a_is_smaller,
  output [4:0] abs_difference
);

  wire [4:0] subtractor_1_out, subtractor_2_out;

  Subtractor #(.width(5)) subtractor_1 (
    .a(exponent_a), .b(exponent_b), .out(subtractor_1_out), .bout(a_is_smaller));  // open: bin
  Multiplexer #(.width(5)) multiplexer_1 (
    .in0(exponent_a), .in1(exponent_b), .out(current_big_exponent), .sel(a_is_smaller));
  Subtractor #(.width(5)) subtractor_2 (
    .a({5{1'b0}}), .b(subtractor_1_out), .out(subtractor_2_out));  // open: bin, bout
  Multiplexer #(.width(5)) multiplexer_2 (
    .in0(subtractor_1_out), .in1(subtractor_2_out), .out(abs_difference), .sel(a_is_smaller));
endmodule

module align_significands (
  input  [10:0] sig_a,
  input  a_is_smaller,
  input  [4:0] abs_diff,
  input  [10:0] sig_b,
  output [13:0] alligned_sig_a,
  output [13:0] aligned_sig_b
);

  wire [8:0] multiplexer_1_out, multiplexer_2_out;
  wire [21:0] shifter_1_out, shifter_2_out;

  Shifter #(.shift("lr"), .width(22)) shifter_1 (.in({sig_a, {11{1'b0}}}), .\dist (abs_diff), .out(shifter_1_out));
  Shifter #(.shift("lr"), .width(22)) shifter_2 (.in({sig_b, {11{1'b0}}}), .\dist (abs_diff), .out(shifter_2_out));
  Multiplexer #(.width(22)) multiplexer_1 (
    .in0({sig_a, {11{1'b0}}}), .in1(shifter_1_out), .out({alligned_sig_a[13:1], multiplexer_1_out}),
    .sel(a_is_smaller));
  Multiplexer #(.width(22)) multiplexer_2 (
    .in0(shifter_2_out), .in1({sig_b, {11{1'b0}}}), .out({aligned_sig_b[13:1], multiplexer_2_out}),
    .sel(a_is_smaller));
  or or_1 (alligned_sig_a[0], multiplexer_1_out[0], multiplexer_1_out[1], multiplexer_1_out[2], multiplexer_1_out[3], multiplexer_1_out[4], multiplexer_1_out[5], multiplexer_1_out[6], multiplexer_1_out[7], multiplexer_1_out[8]);
  or or_2 (aligned_sig_b[0], multiplexer_2_out[0], multiplexer_2_out[1], multiplexer_2_out[2], multiplexer_2_out[3], multiplexer_2_out[4], multiplexer_2_out[5], multiplexer_2_out[6], multiplexer_2_out[7], multiplexer_2_out[8]);
endmodule

module add_sub_sig (
  input  sign_of_a,
  input  sign_of_b,
  input  [13:0] a_alligned,
  input  [13:0] b_alligned,
  output result_sign,
  output operation_sign,
  output [13:0] result_sig,
  output [14:0] alu_fraction_in,
  output carry_out
);

  wire adder_1_cout, comparator_1_lt, comparator_2_eq, multiplexer_3_out, not_1_out;
  wire [13:0] adder_1_out, multiplexer_1_out, multiplexer_2_out, subtractor_1_out;

  xor xor_1 (operation_sign, sign_of_a, sign_of_b);
  Comparator #(.mode("unsigned"), .width(14)) comparator_1 (
    .a(a_alligned), .b(b_alligned), .lt(comparator_1_lt));  // open: gt, eq
  Multiplexer #(.width(14)) multiplexer_1 (
    .in0(a_alligned), .in1(b_alligned), .out(multiplexer_1_out), .sel(comparator_1_lt));
  Multiplexer #(.width(14)) multiplexer_2 (
    .in0(b_alligned), .in1(a_alligned), .out(multiplexer_2_out), .sel(comparator_1_lt));
  Adder #(.width(14)) adder_1 (.a(a_alligned), .b(b_alligned), .out(adder_1_out), .cout(adder_1_cout));  // open: cin
  Multiplexer multiplexer_3 (.in0(sign_of_a), .in1(sign_of_b), .out(multiplexer_3_out), .sel(comparator_1_lt));
  Multiplexer multiplexer_4 (.in0(adder_1_cout), .in1(1'b0), .out(alu_fraction_in[14]), .sel(operation_sign));
  Subtractor #(.width(14)) subtractor_1 (
    .a(multiplexer_1_out), .b(multiplexer_2_out), .out(subtractor_1_out));  // open: bin, bout
  Multiplexer #(.width(14)) multiplexer_5 (
    .in0(adder_1_out), .in1(subtractor_1_out), .out(alu_fraction_in[13:0]), .sel(operation_sign));
  and and_1 (result_sign, multiplexer_3_out, not_1_out);
  Comparator #(.mode("unsigned"), .width(15)) comparator_2 (
    .a({15{1'b0}}), .b(alu_fraction_in), .eq(comparator_2_eq));  // open: gt, lt
  not not_1 (not_1_out, comparator_2_eq);

  assign carry_out = alu_fraction_in[14];
  assign result_sig = alu_fraction_in[13:0];

  // Notes on the sheet:
  //   1 if a<b
  //   selects the larger one
  //   selects the smaller one
  //   picks the larger significands sign
endmodule

module normalized (
  input  [14:0] ALU_Fraction_In,
  input  [4:0] Current_Exponent,
  input  result_sign,
  output [13:0] Normalized_Fraction,
  output [4:0] Normalized_Exponent,
  output underflow,
  output overflow
);

  wire adder_1_cout, and_2_out, comparator_1_eq, comparator_2_eq, comparator_2_lt, not_1_out, or_1_out,
       or_2_out, or_3_out, or_4_out, subtractor_1_bout;
  wire [3:0] priority_encoder_1_out, subtractor_2_out, subtractor_3_out;
  wire [4:0] adder_1_out, bit_extender_1_out, bit_extender_2_out, multiplexer_2_out, multiplexer_3_out,
       multiplexer_5_out, subtractor_1_out;
  wire [4:4] subtractor_3_out_2;
  wire [13:0] multiplexer_1_out, multiplexer_4_out, shifter_1_out, shifter_2_out;

  Multiplexer #(.width(14)) multiplexer_1 (
    .in0(shifter_1_out), .in1(ALU_Fraction_In[14:1]), .out(multiplexer_1_out), .sel(ALU_Fraction_In[14]));
  assign bit_extender_1_out = {{4{1'b0}}, ALU_Fraction_In[14]};  // Bit_Extender bit_extender_1
  assign bit_extender_2_out = {{1{1'b0}}, subtractor_2_out};  // Bit_Extender bit_extender_2
  Adder #(.width(5)) adder_1 (
    .a(Current_Exponent), .b(bit_extender_1_out), .out(adder_1_out), .cin(1'b0), .cout(adder_1_cout));
  Subtractor #(.width(5)) subtractor_1 (
    .a(Current_Exponent), .b(bit_extender_2_out), .out(subtractor_1_out), .bin(1'b0), .bout(subtractor_1_bout));
  or or_1 (or_1_out, ALU_Fraction_In[0], ALU_Fraction_In[1], ALU_Fraction_In[2], ALU_Fraction_In[3], ALU_Fraction_In[4], ALU_Fraction_In[5], ALU_Fraction_In[6], ALU_Fraction_In[7], ALU_Fraction_In[8], ALU_Fraction_In[9], ALU_Fraction_In[10], ALU_Fraction_In[11], ALU_Fraction_In[12], ALU_Fraction_In[13], ALU_Fraction_In[14]);
  Multiplexer #(.width(5)) multiplexer_2 (
    .in0(subtractor_1_out), .in1(adder_1_out), .out(multiplexer_2_out), .sel(ALU_Fraction_In[14]));
  Priority_Encoder #(.select(4)) priority_encoder_1 (
    .in0(ALU_Fraction_In[0]), .in1(ALU_Fraction_In[1]), .in2(ALU_Fraction_In[2]), .in3(ALU_Fraction_In[3]),
    .in4(ALU_Fraction_In[4]), .in5(ALU_Fraction_In[5]), .in6(ALU_Fraction_In[6]), .in7(ALU_Fraction_In[7]),
    .in8(ALU_Fraction_In[8]), .in9(ALU_Fraction_In[9]), .in10(ALU_Fraction_In[10]),
    .in11(ALU_Fraction_In[11]), .in12(ALU_Fraction_In[12]), .in13(ALU_Fraction_In[13]), .in14(1'b0),
    .in15(1'b0), .out(priority_encoder_1_out), .en_in(or_1_out));  // open: gs, en_out
  not not_1 (not_1_out, result_sign);
  Comparator #(.width(5)) comparator_1 (.a(multiplexer_2_out), .b({5{1'b1}}), .eq(comparator_1_eq));  // open: gt, lt
  and and_1 (overflow, or_2_out, not_1_out);
  Subtractor #(.width(4)) subtractor_2 (
    .a(4'b1101), .b(priority_encoder_1_out), .out(subtractor_2_out), .bin(1'b0));  // open: bout
  Multiplexer #(.width(5)) multiplexer_3 (
    .in0({5{1'b0}}), .in1(multiplexer_2_out), .out(multiplexer_3_out), .sel(or_1_out));
  Shifter #(.width(14)) shifter_1 (.in(ALU_Fraction_In[13:0]), .\dist (subtractor_2_out), .out(shifter_1_out));
  Shifter #(.width(14)) shifter_2 (.in(ALU_Fraction_In[13:0]), .\dist (subtractor_3_out), .out(shifter_2_out));
  Subtractor #(.width(5)) subtractor_3 (
    .a(Current_Exponent), .b(5'b00001), .out({subtractor_3_out_2[4], subtractor_3_out}));  // open: bin, bout
  and and_2 (and_2_out, or_1_out, or_3_out);
  or or_2 (or_2_out, adder_1_cout, comparator_1_eq);
  Multiplexer #(.width(14)) multiplexer_4 (
    .in0(multiplexer_1_out), .in1({14{1'b0}}), .out(multiplexer_4_out), .sel(overflow));
  Multiplexer #(.width(5)) multiplexer_5 (
    .in0(multiplexer_3_out), .in1({5{1'b1}}), .out(multiplexer_5_out), .sel(overflow));
  Multiplexer #(.width(14)) multiplexer_6 (
    .in0(multiplexer_4_out), .in1(shifter_2_out), .out(Normalized_Fraction), .sel(underflow));
  Comparator #(.mode("unsigned"), .width(5)) comparator_2 (
    .a(multiplexer_3_out), .b({5{1'b0}}), .eq(comparator_2_eq), .lt(comparator_2_lt));  // open: gt
  or or_3 (or_3_out, or_4_out, subtractor_1_bout);
  Multiplexer multiplexer_7 (.in0(and_2_out), .in1(1'b0), .out(underflow), .sel(ALU_Fraction_In[14]));
  Multiplexer #(.width(5)) multiplexer_8 (
    .in0(multiplexer_5_out), .in1({5{1'b0}}), .out(Normalized_Exponent), .sel(underflow));
  or or_4 (or_4_out, comparator_2_eq, comparator_2_lt);
endmodule
