// Logisim project MIPS_Pipeline_Final.circ as structural Verilog: 9 circuits, main circuit Main
module ALU (
  input  [3:0] A,
  input  [3:0] B,
  input  [2:0] ALUop,
  output [3:0] Result
);

  wire or_2_out, or_3_out;
  wire [3:0] adder_1_out, and_1_out, multiplexer_2_out, multiplexer_3_out, nor_1_out, or_1_out,
       shifter_1_out, shifter_2_out, subtractor_1_out;

  Adder #(.width(4)) adder_1 (.a(A), .b(B), .out(adder_1_out), .cin(1'b0));  // open: cout
  Subtractor #(.width(4)) subtractor_1 (.a(A), .b(B), .out(subtractor_1_out), .bin(1'b0));  // open: bout
  assign and_1_out = A & B;  // AND_Gate and_1, 4 bits wide
  assign or_1_out = A | B;  // OR_Gate or_1, 4 bits wide
  assign nor_1_out = ~(A | B);  // NOR_Gate nor_1, 4 bits wide
  Shifter #(.width(4)) shifter_1 (.in(A), .\dist (B[1:0]), .out(shifter_1_out));
  Shifter #(.shift("lr"), .width(4)) shifter_2 (.in(A), .\dist (B[1:0]), .out(shifter_2_out));
  Multiplexer #(.select(3), .width(4)) multiplexer_1 (
    .in0(adder_1_out), .in1(subtractor_1_out), .in2(and_1_out), .in3(or_1_out), .in4(nor_1_out),
    .in5(multiplexer_2_out), .in6(multiplexer_3_out), .out(Result), .sel(ALUop));  // open: in7
  Multiplexer #(.width(4)) multiplexer_2 (.in0(shifter_1_out), .in1(4'b0000), .out(multiplexer_2_out), .sel(or_2_out));
  or or_2 (or_2_out, B[3], B[2]);
  Multiplexer #(.width(4)) multiplexer_3 (.in0(shifter_2_out), .in1(4'b0000), .out(multiplexer_3_out), .sel(or_3_out));
  or or_3 (or_3_out, B[2], B[3]);
endmodule

module InstrMem (
  input  [7:0] in_1,
  output [15:0] out_2
);

  ROM #(.dataWidth(16)) rom_1 (.addr(in_1), .data(out_2));

  // Notes on the sheet:
  //   contents of rom_1 (hex, n*v repeats v):
  //   a61e 2014 a026 8661 5064 2660 a661 2620 a630 a661 2035
endmodule

module ControlRom (
  input  [3:0] in_1,
  output [11:0] out_2
);

  ROM #(.addrWidth(4), .dataWidth(12)) ControlRom (.addr(in_1), .data(out_2));

  // Notes on the sheet:
  //   contents of ControlRom (hex, n*v repeats v):
  //   605 602 280 606 603 740 21 c03 601 c00 600 c02 c01 11 c04 8
endmodule

module RegFile (
  input  clock,
  input  [3:0] WriteData,
  input  RegWrite,
  input  [3:0] ReadReg1,
  input  [3:0] WriteReg,
  input  [3:0] ReadReg2,
  output [3:0] ReadData1,
  output [3:0] ReadData2
);

  wire and_1_out, and_2_out, and_3_out, and_4_out, and_5_out, and_6_out, decoder_1_out0, decoder_1_out1,
       decoder_1_out2, decoder_1_out3, decoder_1_out4, decoder_1_out5, decoder_1_out6;
  wire [3:0] sp_q, t0_q, t1_q, t2_q, t3_q, t4_q, zero_q;

  Decoder #(.select(4)) decoder_1 (
    .out0(decoder_1_out0), .out1(decoder_1_out1), .out2(decoder_1_out2), .out3(decoder_1_out3),
    .out4(decoder_1_out4), .out5(decoder_1_out5), .out6(decoder_1_out6), .sel(WriteReg), .en(1'b1));  // open: out7, out8, out9, out10, out11, out12, out13, out14, out15
  and and_1 (and_1_out, decoder_1_out1, RegWrite);
  and and_2 (and_2_out, decoder_1_out2, RegWrite);
  and and_3 (and_3_out, decoder_1_out3, RegWrite);
  and and_4 (and_4_out, decoder_1_out4, RegWrite);
  and and_5 (and_5_out, decoder_1_out5, RegWrite);
  and and_6 (and_6_out, decoder_1_out6, RegWrite);
  Register #(.trigger("falling"), .width(4)) t2 (.D(WriteData), .en(and_3_out), .clk(clock), .Q(t2_q), .clr(1'b0));
  Register #(.trigger("falling"), .width(4)) zero (.D(WriteData), .en(1'b0), .clk(clock), .Q(zero_q), .clr(1'b0));
  Register #(.trigger("falling"), .width(4)) t0 (.D(WriteData), .en(and_1_out), .clk(clock), .Q(t0_q), .clr(1'b0));
  Register #(.trigger("falling"), .width(4)) t1 (.D(WriteData), .en(and_2_out), .clk(clock), .Q(t1_q), .clr(1'b0));
  Register #(.trigger("falling"), .width(4)) t3 (.D(WriteData), .en(and_4_out), .clk(clock), .Q(t3_q), .clr(1'b0));
  Register #(.trigger("falling"), .width(4)) t4 (.D(WriteData), .en(and_5_out), .clk(clock), .Q(t4_q), .clr(1'b0));
  Register #(.trigger("falling"), .width(4)) sp (.D(WriteData), .en(and_6_out), .clk(clock), .Q(sp_q), .clr(1'b0));
  Multiplexer #(.select(4), .width(4)) multiplexer_1 (
    .in0(zero_q), .in1(t0_q), .in2(t1_q), .in3(t2_q), .in4(t3_q), .in5(t4_q), .in6(sp_q), .in7(4'b0000),
    .in8(4'b0000), .in9(4'b0000), .in10(4'b0000), .in11(4'b0000), .in12(4'b0000), .in13(4'b0000),
    .in14(4'b0000), .in15(4'b0000), .out(ReadData1), .sel(ReadReg1));
  Multiplexer #(.select(4), .width(4)) multiplexer_2 (
    .in0(zero_q), .in1(t0_q), .in2(t1_q), .in3(t2_q), .in4(t3_q), .in5(t4_q), .in6(sp_q), .in7(4'b0000),
    .in8(4'b0000), .in9(4'b0000), .in10(4'b0000), .in11(4'b0000), .in12(4'b0000), .in13(4'b0000),
    .in14(4'b0000), .in15(4'b0000), .out(ReadData2), .sel(ReadReg2));
endmodule

module Main (
  input  in_1
);

  wire beq, bneq, CLK, hazarddetectionunit_1_if_id_write, hazarddetectionunit_1_pcwrite,
       hazarddetectionunit_1_stall, is_branch, is_immediate, is_jump, j, memtomem_fwd_unit_1_fwd, or_1_out;
  wire [0:0] branch_decision_1_branch;
  wire [1:0] fwd_unit_1_forwarda, fwd_unit_1_forwardb, fwd_unit_2_forwarda, fwd_unit_2_forwardb,
       fwd_unit_2_fwd_sw;
  wire [3:0] alu_1_result, DataMemory_dout, multiplexer_3_out, multiplexer_4_out, multiplexer_6_out,
       multiplexer_8_out, multiplexer_9_out, multiplexer_10_out, multiplexer_11_out, multiplexer_12_out,
       regfile_1_readdata1, regfile_1_readdata2;
  wire [7:0] adder_1_out, adder_2_out, bit_extender_1_out, multiplexer_1_out, PC_q;
  wire [8:0] Controls;
  wire [11:0] controlrom_1_out_2;
  wire [11:8] multiplexer_7_out;
  wire [13:0] MEM_WB_q;
  wire [15:0] instrmem_1_out_2;
  wire [19:0] EX_MEM_q;
  wire [23:0] IF_ID_q, multiplexer_2_out;
  wire [28:0] ID_EX_q;
  wire [28:8] IF_ID_q_2;

  Clock u_CLK (.out(CLK));
  Multiplexer #(.select(2), .width(8)) multiplexer_1 (
    .in0(adder_1_out), .in1(adder_2_out), .in2({IF_ID_q_2[28:25], IF_ID_q_2[15:12]}),
    .out(multiplexer_1_out), .sel({j, branch_decision_1_branch[0]}));  // open: in3
  Register PC (.D(multiplexer_1_out), .en(hazarddetectionunit_1_pcwrite), .clk(CLK), .Q(PC_q), .clr(in_1));
  Adder adder_1 (.a(PC_q), .b(8'h1), .out(adder_1_out), .cin(1'b0));  // open: cout
  InstrMem instrmem_1 (.in_1(PC_q), .out_2(instrmem_1_out_2));
  or or_1 (or_1_out, branch_decision_1_branch[0], j);
  Multiplexer #(.width(24)) multiplexer_2 (
    .in0({instrmem_1_out_2, adder_1_out}), .in1({24{1'b0}}), .out(multiplexer_2_out), .sel(or_1_out));
  Register #(.width(24)) IF_ID (
    .D(multiplexer_2_out), .en(hazarddetectionunit_1_if_id_write), .clk(CLK),
    .Q({IF_ID_q[23:20], IF_ID_q_2[28:25], IF_ID_q_2[15:8], IF_ID_q[7:0]}), .clr(in_1));
  Adder adder_2 (.a(IF_ID_q[7:0]), .b(bit_extender_1_out), .out(adder_2_out), .cin(1'b0));  // open: cout
  assign bit_extender_1_out = {{4{IF_ID_q_2[11]}}, IF_ID_q_2[11:8]};  // Bit_Extender bit_extender_1
  Multiplexer #(.select(2), .width(4)) multiplexer_3 (
    .in0(regfile_1_readdata1), .in1(multiplexer_12_out), .in2(EX_MEM_q[3:0]), .out(multiplexer_3_out),
    .sel(fwd_unit_1_forwarda));  // open: in3
  Multiplexer #(.select(2), .width(4)) multiplexer_4 (
    .in0(regfile_1_readdata2), .in1(multiplexer_12_out), .in2(EX_MEM_q[3:0]), .out(multiplexer_4_out),
    .sel(fwd_unit_1_forwardb));  // open: in3
  RegFile regfile_1 (
    .clock(CLK), .WriteData(multiplexer_12_out), .RegWrite(MEM_WB_q[13]), .ReadReg1(IF_ID_q_2[28:25]),
    .WriteReg(MEM_WB_q[11:8]), .ReadReg2(IF_ID_q_2[15:12]), .ReadData1(regfile_1_readdata1),
    .ReadData2(regfile_1_readdata2));
  Register #(.width(29)) ID_EX (
    .D({IF_ID_q_2[28:25], Controls, IF_ID_q_2[15:8], regfile_1_readdata2, regfile_1_readdata1}), .clk(CLK),
    .Q(ID_EX_q), .clr(in_1));  // open: en
  HazardDetectionUnit hazarddetectionunit_1 (
    .ID_EX_Memread(ID_EX_q[22]), .IF_ID_regrs(IF_ID_q_2[28:25]), .ID_EX_regrt(ID_EX_q[15:12]),
    .IF_ID_regrt(IF_ID_q_2[15:12]), .IF_ID_is_immediate(is_immediate), .is_branch(is_branch),
    .ID_EX_RegWrite(ID_EX_q[24]), .ID_EX_regdest(multiplexer_7_out), .EX_MEM_Memread(EX_MEM_q[13]),
    .EX_MEM_regdest(EX_MEM_q[11:8]), .is_jump(is_jump), .Stall(hazarddetectionunit_1_stall),
    .IF_ID_Write(hazarddetectionunit_1_if_id_write), .PCWrite(hazarddetectionunit_1_pcwrite));
  ControlRom controlrom_1 (
    .in_1(IF_ID_q[23:20]),
    .out_2({controlrom_1_out_2[11:10], is_immediate, controlrom_1_out_2[8:4], is_jump, controlrom_1_out_2[2:0]}));
  Multiplexer #(.width(12)) multiplexer_5 (
    .in0({controlrom_1_out_2[11:10], is_immediate, controlrom_1_out_2[8:4], is_jump, controlrom_1_out_2[2:0]}),
    .in1({12{1'b0}}),
    .out({Controls[4], Controls[8], Controls[3], Controls[6:5], Controls[7], beq, bneq, j, Controls[2:0]}),
    .sel(hazarddetectionunit_1_stall));
  FWD_Unit fwd_unit_1 (
    .MEM_WB_rd(MEM_WB_q[11:8]), .ID_EX_src1(IF_ID_q_2[28:25]), .EX_Mem_rd(EX_MEM_q[11:8]),
    .EX_MEM_Regwrite(EX_MEM_q[15]), .MEM_WB_Regwrite(MEM_WB_q[13]), .ID_EX_src2(IF_ID_q_2[15:12]),
    .is_immediate(1'b0), .ForwardA(fwd_unit_1_forwarda), .ForwardB(fwd_unit_1_forwardb));  // open: FWD_SW
  Multiplexer #(.width(4)) multiplexer_6 (
    .in0(ID_EX_q[7:4]), .in1(ID_EX_q[11:8]), .out(multiplexer_6_out), .sel(ID_EX_q[19]));
  branch_decision branch_decision_1 (
    .beq(beq), .bneq(bneq), .Data1(multiplexer_3_out), .Data2(multiplexer_4_out),
    .Branch(branch_decision_1_branch[0]));
  Multiplexer #(.width(4)) multiplexer_7 (
    .in0(ID_EX_q[15:12]), .in1(ID_EX_q[11:8]), .out(multiplexer_7_out), .sel(ID_EX_q[20]));
  or or_2 (is_branch, controlrom_1_out_2[4], controlrom_1_out_2[5]);
  Multiplexer #(.select(2), .width(4)) multiplexer_8 (
    .in0(ID_EX_q[3:0]), .in1(multiplexer_12_out), .in2(EX_MEM_q[3:0]), .out(multiplexer_8_out),
    .sel(fwd_unit_2_forwarda));  // open: in3
  Multiplexer #(.select(2), .width(4)) multiplexer_9 (
    .in0(multiplexer_6_out), .in1(multiplexer_12_out), .in2(EX_MEM_q[3:0]), .out(multiplexer_9_out),
    .sel(fwd_unit_2_forwardb));  // open: in3
  Multiplexer #(.select(2), .width(4)) multiplexer_10 (
    .in0(ID_EX_q[7:4]), .in1(multiplexer_12_out), .in2(EX_MEM_q[3:0]), .out(multiplexer_10_out),
    .sel(fwd_unit_2_fwd_sw));  // open: in3
  ALU alu_1 (.A(multiplexer_8_out), .B(multiplexer_9_out), .ALUop(ID_EX_q[18:16]), .Result(alu_1_result));
  FWD_Unit fwd_unit_2 (
    .MEM_WB_rd(MEM_WB_q[11:8]), .ID_EX_src1(ID_EX_q[28:25]), .EX_Mem_rd(EX_MEM_q[11:8]),
    .EX_MEM_Regwrite(EX_MEM_q[15]), .MEM_WB_Regwrite(MEM_WB_q[13]), .ID_EX_src2(ID_EX_q[15:12]),
    .is_immediate(ID_EX_q[19]), .ForwardA(fwd_unit_2_forwarda), .FWD_SW(fwd_unit_2_fwd_sw),
    .ForwardB(fwd_unit_2_forwardb));
  Register #(.width(20)) EX_MEM (
    .D({ID_EX_q[15:12], ID_EX_q[24:21], multiplexer_7_out, multiplexer_10_out, alu_1_result}), .clk(CLK),
    .Q(EX_MEM_q), .clr(in_1));  // open: en
  RAM #(.addrWidth(4), .asyncread("true"), .dataWidth(4)) DataMemory (
    .addr(EX_MEM_q[3:0]), .we(EX_MEM_q[12]), .oe(EX_MEM_q[13]), .clk(CLK), .din(multiplexer_11_out),
    .dout(DataMemory_dout));
  Multiplexer #(.width(4)) multiplexer_11 (
    .in0(EX_MEM_q[7:4]), .in1(multiplexer_12_out), .out(multiplexer_11_out), .sel(memtomem_fwd_unit_1_fwd));
  MemtoMem_fwd_unit memtomem_fwd_unit_1 (
    .MEM_WB_RegWrite(MEM_WB_q[13]), .MEM_WB_rd(MEM_WB_q[11:8]), .EX_MEM_rt(EX_MEM_q[19:16]),
    .fwd(memtomem_fwd_unit_1_fwd));
  Register #(.width(14)) MEM_WB (
    .D({EX_MEM_q[15:14], EX_MEM_q[11:8], DataMemory_dout, EX_MEM_q[3:0]}), .clk(CLK), .Q(MEM_WB_q), .clr(in_1));  // open: en
  Multiplexer #(.width(4)) multiplexer_12 (
    .in0(MEM_WB_q[3:0]), .in1(MEM_WB_q[7:4]), .out(multiplexer_12_out), .sel(MEM_WB_q[12]));

  // Other names for the same wires on the sheet: R = in_1

  // Notes on the sheet:
  //   PCsrc
  //   Restart
  //   src1
  //   ALUSrc
  //   RegDst
  //   src2
  //   6-MemtoReg
  //   8-Memread
  //   7-Memwrite
  //   9-ALUSrc
  //   mem_wb_rd
  //   ex_mem_rd
  //   7-4: Data that will be written into memory
  //   MemtoReg
endmodule

module FWD_Unit (
  input  [3:0] MEM_WB_rd,
  input  [3:0] ID_EX_src1,
  input  [3:0] EX_Mem_rd,
  input  EX_MEM_Regwrite,
  input  MEM_WB_Regwrite,
  input  [3:0] ID_EX_src2,
  input  is_immediate,
  output [1:0] ForwardA,
  output [1:0] FWD_SW,
  output [1:0] ForwardB
);

  wire and_1_out, and_2_out, comparator_1_eq, comparator_2_eq, comparator_3_eq, comparator_4_eq,
       comparator_5_eq, comparator_6_eq, not_1_out, not_2_out, not_3_out;
  wire [1:0] and_4_out, and_6_out, and_8_out;

  not not_1 (not_1_out, comparator_1_eq);
  Comparator #(.mode("unsigned"), .width(4)) comparator_1 (
    .a(MEM_WB_rd), .b(4'b0000), .eq(comparator_1_eq));  // open: gt, lt
  not not_2 (not_2_out, comparator_2_eq);
  Comparator #(.mode("unsigned"), .width(4)) comparator_2 (
    .a(4'b0000), .b(EX_Mem_rd), .eq(comparator_2_eq));  // open: gt, lt
  and and_1 (and_1_out, not_2_out, EX_MEM_Regwrite);
  and and_2 (and_2_out, not_1_out, MEM_WB_Regwrite);
  Comparator #(.mode("unsigned"), .width(4)) comparator_3 (
    .a(MEM_WB_rd), .b(ID_EX_src1), .eq(comparator_3_eq));  // open: gt, lt
  Comparator #(.mode("unsigned"), .width(4)) comparator_4 (
    .a(ID_EX_src1), .b(EX_Mem_rd), .eq(comparator_4_eq));  // open: gt, lt
  Comparator #(.mode("unsigned"), .width(4)) comparator_5 (
    .a(MEM_WB_rd), .b(ID_EX_src2), .eq(comparator_5_eq));  // open: gt, lt
  Comparator #(.mode("unsigned"), .width(4)) comparator_6 (
    .a(ID_EX_src2), .b(EX_Mem_rd), .eq(comparator_6_eq));  // open: gt, lt
  and and_3 (and_4_out[1], and_1_out, comparator_4_eq);
  and and_4 (and_4_out[0], comparator_3_eq, and_2_out);
  and and_5 (and_6_out[1], and_1_out, comparator_6_eq);
  and and_6 (and_6_out[0], comparator_5_eq, and_2_out);
  not not_3 (not_3_out, is_immediate);
  and and_7 (and_8_out[1], and_6_out[1], not_3_out);
  and and_8 (and_8_out[0], and_6_out[0], not_3_out);
  Multiplexer #(.select(2), .width(2)) multiplexer_1 (
    .in0(2'b00), .in1(2'b01), .in2(2'b10), .in3(2'b10), .out(ForwardA), .sel(and_4_out));
  Multiplexer #(.select(2), .width(2)) multiplexer_2 (
    .in0(2'b00), .in1(2'b01), .in2(2'b10), .in3(2'b10), .out(ForwardB), .sel(and_8_out));
  Multiplexer #(.select(2), .width(2)) multiplexer_3 (
    .in0(2'b00), .in1(2'b01), .in2(2'b10), .in3(2'b10), .out(FWD_SW), .sel(and_6_out));
endmodule

module HazardDetectionUnit (
  input  ID_EX_Memread,
  input  [3:0] IF_ID_regrs,
  input  [3:0] ID_EX_regrt,
  input  [3:0] IF_ID_regrt,
  input  IF_ID_is_immediate,
  input  is_branch,
  input  ID_EX_RegWrite,
  input  [3:0] ID_EX_regdest,
  input  EX_MEM_Memread,
  input  [3:0] EX_MEM_regdest,
  input  is_jump,
  output Stall,
  output IF_ID_Write,
  output PCWrite
);

  wire and_1_out, and_2_out, and_3_out, and_4_out, comparator_1_eq, comparator_2_eq, comparator_3_eq,
       comparator_4_eq, comparator_5_eq, comparator_6_eq, comparator_7_eq, comparator_8_eq, comparator_9_eq,
       multiplexer_1_out, not_1_out, not_2_out, not_3_out, not_4_out, not_5_out, or_1_out, or_2_out,
       or_3_out, or_4_out;

  not not_1 (not_1_out, IF_ID_is_immediate);
  Comparator #(.mode("unsigned"), .width(4)) comparator_1 (
    .a(ID_EX_regdest), .b(4'b0000), .eq(comparator_1_eq));  // open: gt, lt
  Comparator #(.mode("unsigned"), .width(4)) comparator_2 (
    .a(EX_MEM_regdest), .b(4'b0000), .eq(comparator_2_eq));  // open: gt, lt
  not not_2 (not_2_out, comparator_3_eq);
  Comparator #(.mode("unsigned"), .width(4)) comparator_3 (
    .a(ID_EX_regrt), .b(4'b0000), .eq(comparator_3_eq));  // open: gt, lt
  Comparator #(.mode("unsigned"), .width(4)) comparator_4 (
    .a(IF_ID_regrs), .b(ID_EX_regrt), .eq(comparator_4_eq));  // open: gt, lt
  Comparator #(.mode("unsigned"), .width(4)) comparator_5 (
    .a(ID_EX_regrt), .b(IF_ID_regrt), .eq(comparator_5_eq));  // open: gt, lt
  not not_3 (not_3_out, comparator_1_eq);
  Comparator #(.mode("unsigned"), .width(4)) comparator_6 (
    .a(IF_ID_regrs), .b(ID_EX_regdest), .eq(comparator_6_eq));  // open: gt, lt
  Comparator #(.mode("unsigned"), .width(4)) comparator_7 (
    .a(ID_EX_regdest), .b(IF_ID_regrt), .eq(comparator_7_eq));  // open: gt, lt
  not not_4 (not_4_out, comparator_2_eq);
  Comparator #(.mode("unsigned"), .width(4)) comparator_8 (
    .a(IF_ID_regrs), .b(EX_MEM_regdest), .eq(comparator_8_eq));  // open: gt, lt
  Comparator #(.mode("unsigned"), .width(4)) comparator_9 (
    .a(EX_MEM_regdest), .b(IF_ID_regrt), .eq(comparator_9_eq));  // open: gt, lt
  and and_1 (and_1_out, comparator_5_eq, not_1_out);
  or or_1 (or_1_out, comparator_6_eq, comparator_7_eq);
  or or_2 (or_2_out, comparator_8_eq, comparator_9_eq);
  or or_3 (or_3_out, comparator_4_eq, and_1_out);
  and and_2 (and_2_out, ID_EX_RegWrite, not_3_out, or_1_out);
  and and_3 (and_3_out, EX_MEM_Memread, not_4_out, or_2_out);
  and and_4 (and_4_out, ID_EX_Memread, not_2_out, or_3_out);
  or or_4 (or_4_out, and_2_out, and_3_out);
  not not_5 (not_5_out, is_jump);
  Multiplexer multiplexer_1 (.in0(and_4_out), .in1(or_4_out), .out(multiplexer_1_out), .sel(is_branch));
  and and_5 (Stall, multiplexer_1_out, not_5_out);
  not not_6 (IF_ID_Write, Stall);

  assign PCWrite = IF_ID_Write;
endmodule

module MemtoMem_fwd_unit (
  input  MEM_WB_RegWrite,
  input  [3:0] MEM_WB_rd,
  input  [3:0] EX_MEM_rt,
  output fwd
);

  wire and_1_out, comparator_1_eq, comparator_2_eq, not_1_out;

  Comparator #(.mode("unsigned"), .width(4)) comparator_1 (
    .a(MEM_WB_rd), .b(4'b0000), .eq(comparator_1_eq));  // open: gt, lt
  Comparator #(.mode("unsigned"), .width(4)) comparator_2 (
    .a(MEM_WB_rd), .b(EX_MEM_rt), .eq(comparator_2_eq));  // open: gt, lt
  not not_1 (not_1_out, comparator_1_eq);
  and and_1 (and_1_out, MEM_WB_RegWrite, not_1_out);
  and and_2 (fwd, and_1_out, comparator_2_eq);
endmodule

module branch_decision (
  input  beq,
  input  bneq,
  input  [3:0] Data1,
  input  [3:0] Data2,
  output Branch
);

  wire and_1_out, and_2_out, comparator_1_eq, not_1_out;
  wire [3:0] xor_1_out;

  assign xor_1_out = Data1 ^ Data2;  // XOR_Gate xor_1, 4 bits wide
  Comparator #(.mode("unsigned"), .width(4)) comparator_1 (
    .a(xor_1_out), .b(4'b0000), .eq(comparator_1_eq));  // open: gt, lt
  not not_1 (not_1_out, comparator_1_eq);
  and and_1 (and_1_out, beq, comparator_1_eq);
  and and_2 (and_2_out, bneq, not_1_out);
  or or_1 (Branch, and_1_out, and_2_out);
endmodule
